// Logisim project Exercise1.circ as structural Verilog: 1 circuit, main circuit main
module main (
  input  in_1,
  input  in_2,
  input  in_3,
  input  in_4
);

  wire nand_1_out, nand_2_out, nor_1_out, not_1_out, not_2_out;

  not not_1 (not_1_out, in_3);
  not not_2 (not_2_out, in_4);
  nand nand_1 (nand_1_out, in_2, not_1_out);
  nor nor_1 (nor_1_out, nand_1_out, not_2_out);
  LED led_1 (.in(nand_2_out));
  nand nand_2 (nand_2_out, in_1, nor_1_out);
endmodule
