// Logisim project Exercise4.circ as structural Verilog: 1 circuit, main circuit main
module main (
  input  in_1
);

  wire clock_1_out, j_k_ff_1_q, j_k_ff_2_q, nand_1_out, nand_2_out, nand_3_out, nand_4_out;

  nand nand_1 (nand_1_out, j_k_ff_2_q, in_1);
  nand nand_2 (nand_2_out, j_k_ff_2_q, nand_1_out);
  nand nand_3 (nand_3_out, nand_1_out, in_1);
  Clock clock_1 (.out(clock_1_out));
  nand nand_4 (nand_4_out, nand_2_out, nand_3_out);
  J_K_Flip_Flop j_k_ff_1 (
    .J(nand_4_out), .clk(clock_1_out), .K(nand_4_out), .Q(j_k_ff_1_q));  // open: Qn, preset, en, reset
  J_K_Flip_Flop j_k_ff_2 (.J(1'b1), .clk(clock_1_out), .K(1'b1), .Q(j_k_ff_2_q));  // open: Qn, preset, en, reset
  LED led_1 (.in(j_k_ff_1_q));
  LED led_2 (.in(j_k_ff_2_q));
endmodule
