// Logisim project task5.circ as structural Verilog: 1 circuit, main circuit main
module main (
  input  in_1
);

  wire clock_1_out, d_ff_1_q, d_ff_1_qn, d_ff_2_q, d_ff_2_qn, nand_1_out, nand_2_out, nand_3_out, nor_1_out,
       not_1_out;

  Clock clock_1 (.out(clock_1_out));
  not not_1 (not_1_out, in_1);
  nand nand_1 (nand_1_out, d_ff_2_q, not_1_out);
  nand nand_2 (nand_2_out, d_ff_1_q, in_1, d_ff_2_qn);
  nand nand_3 (nand_3_out, nand_1_out, nand_2_out);
  D_Flip_Flop d_ff_1 (.clk(clock_1_out), .D(nand_3_out), .Q(d_ff_1_q), .Qn(d_ff_1_qn));  // open: preset, en, reset
  LED led_1 (.in(d_ff_1_q));
  D_Flip_Flop d_ff_2 (.clk(clock_1_out), .D(in_1), .Q(d_ff_2_q), .Qn(d_ff_2_qn));  // open: preset, en, reset
  LED led_2 (.in(d_ff_2_q));
  nor nor_1 (nor_1_out, d_ff_1_qn, d_ff_2_qn);
  LED led_3 (.in(nor_1_out));
endmodule
